# Fritzing sketch sketch (saved by Fritzing 0.9.3b)

parts:
  M1 = Spresense ext board
  BUTTON2 = Waterproof Pushbutton (green)
  SP1 = SPEAKER [package=pcb_mount_speaker]  # not connected

nets:
  N1: M1.GND, BUTTON2.no_name_yet#1, BUTTON2.no_name_yet#5
  N2: M1.2, BUTTON2.no_name_yet#4
  N3: M1.13, BUTTON2.no_name_yet#2

custom parts:
  Waterproof Pushbutton (green): Waterproof Illuminated Pushbutton (green)
